# Fritzing sketch first_breadboard (saved by Fritzing 1.0.7)
breadboards: 1

parts:
  Mod2 = Microbit
  LED1 = LED - 5mm [color="Red (633nm)" current=0.030A package="5 mm [THT]"]
  R1 = Resistor [tolerance=±5% power=0.25W resistance=47 package=THT]

nets:
  N1: Mod2.P2-bot, R1.Pin_0
  N2: Mod2.GND-19, LED1.cathode
  N3: LED1.anode, R1.Pin_1

custom parts:
  Microbit: BBC Microbit Fritzing part. July 2020 modify to match the xxx breakout board from yyyy. Remove pcb view as unused (this is a breakout board) and add all the connectors on the breakout board (not all of which I know the purpose of at the moment.)
